# Fritzing sketch QuitaSicote3000_conexiones (saved by Fritzing 1.0.6)

parts:
  PSU = Fuente 12 V / 20 A (PSU)
  TB12 = Barra de distribución +12 V (TB12)
  TBG = Barra de tierra en estrella (TBG)
  REG_A = REG_A buck 12→5 V ≥2 A (control + HMI)
  REG_B = REG_B buck 12→5 V ≥1 A (SIS)
  HMI = HMI ESP32-32E pantalla 3.2"
  MCU_C = ESP32 DevKit V1 — CONTROL (MCU_C)
  MCU_S = ESP32 DevKit V1 — SIS (MCU_S, girada 180°)
  TC1 = TC1 termopar K (aire de recámara)
  TC2 = TC2 termopar K (salida del PTC)
  M1 = M1 módulo MAX6675 (TC1)
  M2 = M2 módulo MAX6675 (TC2)
  S1 = S1 módulo SHT31 (T/HR, I2C 0x44)
  S2 = S2 módulo SGP40 (VOC, I2C 0x59)
  SW1 = SW1 limit switch de puerta SPDT
  TH1 = TH1 termostato bimetálico 80 °C NC
  RL1 = RL1 módulo relé 12 V 30 A (permiso PTC)
  PTC = PTC calefactor 100 W / 12 V
  SSR1 = SSR1 DC-DC (PTC, lado bajo)
  RL2 = RL2 módulo relé 12 V (apagar FAN_P)
  RM1 = RM1 módulo 2 relés (K1=RL3, K2=RL4)
  FAN_P = FAN_P ventilador 12 V (ventilador PTC)
  FAN_C = FAN_C ventilador 12 V (circulación)
  SSR2 = SSR2 DC-DC (FAN_C, lado bajo)
  FAN_B = FAN_B ventilador 12 V (cámara circuitos)

nets:
  N1: PSU.V−, TBG.1, TBG.2, TBG.5, TBG.12, TBG.14, TBG.16, TBG.17, TBG.18, TBG.19, TBG.20, REG_A.IN−, REG_B.IN−, RL1.DC−, SSR1.1_OUT−, SSR1.4_IN−, RL2.DC−, RM1.DC−, RM1.NA2, FAN_P.−, SSR2.1_OUT−, SSR2.4_IN−, FAN_B.−
  N2: PSU.V+, TB12.1, TB12.8, TB12.9, TB12.10, TB12.11, TB12.14, REG_A.IN+, REG_B.IN+, TH1.1, RL1.DC+, RL2.DC+, RL2.COM, RM1.DC+, RM1.COM1, FAN_C.+, FAN_B.+
  5V: REG_A.OUT+, HMI.5V, MCU_C.VIN
  GND: REG_A.OUT−, HMI.GND, MCU_C.GND, M1.GND, M2.GND, S1.GND, S2.GND
  N3: REG_B.OUT+, MCU_S.VIN
  N4: REG_B.OUT−, MCU_S.GND, SW1.COM
  N5: HMI.IO25_(TX2), MCU_C.D35
  N6: HMI.IO32_(RX2), MCU_C.D4
  N7: MCU_C.D23, M1.CS
  N8: MCU_C.D22, S1.SCL, S2.SCL
  N9: MCU_C.D21, S1.SDA, S2.SDA
  N10: MCU_C.D19, M1.SO, M2.SO
  N11: MCU_C.D18, M1.SCK, M2.SCK
  N12: MCU_C.TX2_(17), MCU_S.RX2_(16)
  N13: MCU_C.RX2_(16), MCU_S.TX2_(17)
  VCC: MCU_C.3V3, M1.VCC, M2.VCC, S1.VIN, S2.VIN
  N14: MCU_C.D32, MCU_S.D32, SW1.NA
  N15: MCU_C.D33, MCU_S.D33, SW1.NC
  N16: MCU_C.D25, SSR1.3_IN+
  N17: MCU_C.D26, SSR2.3_IN+
  N18: MCU_C.D27, RL2.IN
  N19: MCU_C.D13, M2.CS
  N20: MCU_S.D27, RM1.IN2
  N21: MCU_S.D26, RM1.IN1
  N22: MCU_S.D25, RL1.IN
  N23: TC1.+, M1.+
  N24: TC1.−, M1.−
  N25: TC2.+, M2.+
  N26: TC2.−, M2.−
  N27: TH1.2, RL1.COM
  N28: RL1.NA, PTC.+
  N29: PTC.−, SSR1.2_OUT+
  N30: RL2.NC, RM1.NC1, FAN_P.+
  N31: RM1.COM2, FAN_C.−, SSR2.2_OUT+

notes:
  QuitaSicote3000 · diagrama de conexiones
  Código de colores de cables:
  ■ ROJO = +12 V (incluye tramos conmutados de 12 V).
  ■ ROJO con bandas = retorno de carga hacia el SSR/relé del lado bajo (no es GND).
  ■ NARANJA = 5 V (salida de los buck REG_A / REG_B).
  ■ NARANJA con bandas = 3,3 V del pin 3V3 del ESP32 de control (sensores).
  ■ AZUL = señales (GPIO, SPI, I2C, UART, puerta, termopares).
  ■ NEGRO = GND / COM (sólo tierra).
  Notas
  • Fuente: pinout/*.md y PLAN-MAESTRO §5 del repositorio (TH1 cableado con la opción T1).
  • Dos buck: REG_A (control + HMI) y REG_B (SIS, independiente).
  • Rama del PTC y cable principal en 12 AWG (≈8,3 A en régimen, sin fusibles).
  • FAN_P: contactos NC de RL2 y RL3 (RM1-K1) en paralelo. FAN_C: NA de RL4 (RM1-K2) en paralelo con SSR2.
  • Los COM de relé llevan 12 V o el retorno de carga, por eso no van en negro.
  • MCU_S está dibujada girada 180° (USB a la izquierda).
  • HMI: verificar el orden del conector I2C de 4 pines; su 3V3 no se conecta.
  • Entrada 120 V CA de la PSU (L, N, ⏚) no dibujada.

custom parts:
  Fuente 12 V / 20 A (PSU): Fuente conmutada externa 12 V 20 A
  Barra de distribución +12 V (TB12): Bornera/barra de distribución +12 V
  Barra de tierra en estrella (TBG): Bornera/barra de tierra (estrella)
  HMI ESP32-32E pantalla 3.2": Placa ESP32-32E 3.2" (LCDwiki E32R32P). Orden del conector I2C: VERIFICAR
  ESP32 DevKit V1 — CONTROL (MCU_C): ESP32 DevKit V1 DOIT 30 pines, nodo de control
  ESP32 DevKit V1 — SIS (MCU_S, girada 180°): ESP32 DevKit V1 DOIT 30 pines, nodo SIS. Dibujada girada 180°
